// Logisim project exam2Logisim.circ as structural Verilog
module q16_Nand (
  input  A,
  input  B,
  output X
);

  nand nand_1 (X, A, B);
endmodule

module q17_OR (
  input  A,
  input  B,
  output X
);

  or or_1 (X, A, B);
endmodule

module q18__a____b___c_______a_____b____c (
  input  A,
  input  B,
  input  C,
  output X
);

  wire and_1_out, and_2_out, not_1_out, not_2_out, not_3_out, not_4_out;

  not not_1 (not_1_out, A);
  not not_2 (not_2_out, B);
  not not_3 (not_3_out, C);
  not not_4 (not_4_out, C);
  and and_1 (and_1_out, not_1_out, not_2_out, not_3_out);
  and and_2 (and_2_out, A, B, not_4_out);
  or or_1 (X, and_1_out, and_2_out);
endmodule

module q19_NOR (
  input  in_1,
  input  in_2,
  output out_3
);

  nor nor_1 (out_3, in_1, in_2);

  // Notes on the sheet:
  //   (A + B)'
endmodule

module q20_OR (
  input  A,
  input  B,
  output X
);

  or or_1 (X, A, B);
endmodule

module q21___A_x_B_____A_B (
  input  A,
  input  B,
  output out_3
);

  wire and_1_out, not_1_out, or_1_out;

  and and_1 (and_1_out, A, B);
  or or_1 (or_1_out, A, not_1_out);
  not not_1 (not_1_out, B);
  nor nor_1 (out_3, and_1_out, or_1_out);

  // Notes on the sheet:
  //   X = ((A X B) + (A +B'))'
endmodule

module q22_A____B (
  input  A,
  input  B,
  output out_3
);

  wire not_1_out, not_2_out;

  not not_1 (not_1_out, A);
  not not_2 (not_2_out, B);
  or or_1 (out_3, not_1_out, not_2_out);
endmodule

module q29 (
  input  in_1,
  input  in_2,
  input  in_3,
  input  in_4,
  output out_5,
  output out_6,
  output out_7
);

  wire q29_half_adder_1_carry;

  q29_Half_Adder q29_half_adder_1 (.A(in_4), .B(in_2), .Sum(out_7), .Carry(q29_half_adder_1_carry));
  q29_Full_Adder q29_full_adder_1 (
    .A(in_3), .B(in_1), .Carry_In(q29_half_adder_1_carry), .Sum(out_6), .Carry_Out(out_5));
endmodule

// HA
module q29_Half_Adder (
  input  A,
  input  B,
  output Sum,
  output Carry
);

  xor xor_1 (Sum, A, B);
  and and_1 (Carry, B, A);
endmodule

// FA
module q29_Full_Adder (
  input  Carry_In,
  input  A,
  input  B,
  output Sum,
  output Carry_Out
);

  wire and_1_out, and_2_out, xor_1_out;

  xor xor_1 (xor_1_out, A, B);
  and and_1 (and_1_out, B, A);
  xor xor_2 (Sum, xor_1_out, Carry_In);
  and and_2 (and_2_out, Carry_In, xor_1_out);
  or or_1 (Carry_Out, and_2_out, and_1_out);
endmodule

module q30 (
  input  D0,
  input  D1,
  input  S,
  output Carry_Out
);

  wire n2_1_mux_1_f, not_1_out;

  not not_1 (not_1_out, D0);
  _2_1_Mux u_2_1_mux_1 (.D0(D0), .D1(D1), .S0(S), .F(n2_1_mux_1_f));
  and and_1 (Carry_Out, not_1_out, n2_1_mux_1_f, D1);
endmodule

// Mux
module _2_1_Mux (
  input  D0,
  input  D1,
  input  S0,
  output F
);

  wire and_1_out, and_2_out, not_1_out;

  not not_1 (not_1_out, S0);
  and and_1 (and_1_out, D1, S0);
  and and_2 (and_2_out, D0, not_1_out);
  or or_1 (F, and_2_out, and_1_out);
endmodule

module And (
  input  A,
  input  B,
  output \output 
);

  and and_1 (\output , A, B);
endmodule

module q12 (
  input  A,
  input  B,
  input  C,
  output X
);

  wire and_1_out, and_2_out, not_1_out, not_2_out, not_3_out, not_4_out;

  not not_1 (not_1_out, A);
  not not_2 (not_2_out, C);
  not not_3 (not_3_out, B);
  not not_4 (not_4_out, C);
  and and_1 (and_1_out, not_1_out, not_2_out);
  and and_2 (and_2_out, not_3_out, not_4_out);
  or or_1 (X, and_1_out, and_2_out);
endmodule
